# Fritzing sketch Devre10_7segmangosterge (saved by Fritzing 0.9.3b)
breadboards: 1

parts:
  U1 = POT [package=pot_alpha_rv16af-20]
  7_Segment1 = 7 Segment Display
  U2 = ESP32-38PinWide [part_number=ESP32-38PinWide]

nets:
  N1: U1.A, U2.3.3
  N2: U1.S, U2.GPIO34
  N3: U1.E, 7_Segment1.common_anode, U2.GND
  N4: 7_Segment1.Segment_E, U2.GPIO18
  N5: 7_Segment1.Segment_D, U2.GPIO19
  N6: 7_Segment1.Segment_C, U2.GPIO21
  N7: 7_Segment1.Segment_B, U2.GPIO22
  N8: 7_Segment1.Segment_A, U2.GPIO23
  N9: 7_Segment1.Segment_F, U2.GPIO5
  N10: 7_Segment1.Segment_G, U2.GPIO17

custom parts:
  ESP32-38PinWide: Generic 38-Pin ESP32 with wide format (only access to one side of pins on a breadboard) based on Stephen Lilley's HiLetgo ESP-WROOM-32 ESP32 ESP-32S Development Board.
