# Fritzing sketch Devre11_UartLed (saved by Fritzing 0.9.3b)
breadboards: 1

parts:
  U1 = ESP32-38PinWide [part_number=ESP32-38PinWide]
  Parça3 = FTDI Basic Programmer
  LED1 = smd LED [color="Red (633nm)" package="1206 [SMD]"]
  LED2 = smd LED [color="Red (633nm)" package="1206 [SMD]"]

nets:
  N1: U1.GPIO32, Parça3.TXO
  N2: U1.GPIO33, Parça3.RXI
  GND: U1.GND, Parça3.GND, LED1.cathode, LED2.cathode
  N3: U1.GPIO18, LED2.anode
  N4: U1.GPIO19, LED1.anode

custom parts:
  ESP32-38PinWide: Generic 38-Pin ESP32 with wide format (only access to one side of pins on a breadboard) based on Stephen Lilley's HiLetgo ESP-WROOM-32 ESP32 ESP-32S Development Board.
