# Fritzing sketch Devre12_RTCI2C (saved by Fritzing 0.9.3b)
breadboards: 1

parts:
  Parça1 = Logic Level Converter
  Parça2 = Real Time Clock Module - DS1307 RTC Breakout Board
  U1 = ESP32-38PinWide [part_number=ESP32-38PinWide]

nets:
  N1: Parça1.TX2_LV, U1.GPIO12
  N2: Parça1.RX2_LV, U1.GPIO13
  GND: Parça1.GND, Parça2.GND, U1.GPIO11
  N3: Parça1.LV, U1.3.3
  5V: Parça1.HV, Parça2.5V, U1.VIN
  N4: Parça1.RX2_HV, Parça2.SCL
  N5: Parça1.TX2_HV, Parça2.SDA

custom parts:
  ESP32-38PinWide: Generic 38-Pin ESP32 with wide format (only access to one side of pins on a breadboard) based on Stephen Lilley's HiLetgo ESP-WROOM-32 ESP32 ESP-32S Development Board.
