# Fritzing sketch Devre2_TrafikIsigi (saved by Fritzing 0.9.3b)
breadboards: 1

parts:
  U1 = ESP32-38PinWide [part_number=ESP32-38PinWide]
  LED1 = smd LED [color="Green (555nm)" package="0603 [SMD]"]
  LED2 = smd LED [color="Yellow (595nm)" package="0603 [SMD]"]
  LED3 = smd LED [color="Red (633nm)" package="0603 [SMD]"]
  R1 = Resistor [tolerance=±5% resistance=330 package=THT]
  R2 = Resistor [tolerance=±5% resistance=330 package=THT]
  R3 = Resistor [tolerance=±5% resistance=330 package=THT]

nets:
  N1: U1.GPIO5, R2.Pin_1
  N2: U1.GPIO18, R1.Pin_1
  N3: U1.GPIO19, R3.Pin_1
  N4: U1.GND, LED1.cathode, LED2.cathode, LED3.cathode
  N5: LED1.anode, R3.Pin_0
  N6: LED2.anode, R1.Pin_0
  N7: LED3.anode, R2.Pin_0

custom parts:
  ESP32-38PinWide: Generic 38-Pin ESP32 with wide format (only access to one side of pins on a breadboard) based on Stephen Lilley's HiLetgo ESP-WROOM-32 ESP32 ESP-32S Development Board.
