# Fritzing sketch Devre4_ButonLedFiltre (saved by Fritzing 0.9.3b)
breadboards: 1

parts:
  U1 = ESP32-38PinWide [part_number=ESP32-38PinWide]
  LED1 = smd LED [color="Green (555nm)" package="0603 [SMD]"]
  LED2 = smd LED [color="Yellow (595nm)" package="0603 [SMD]"]
  LED3 = smd LED [color="Red (633nm)" package="0603 [SMD]"]
  R1 = Resistor [tolerance=±5% resistance=330 package=THT]
  R2 = Resistor [tolerance=±5% resistance=330 package=THT]
  R3 = Resistor [tolerance=±5% resistance=330 package=THT]
  R4 = Resistor [tolerance=±5% resistance=1k package=THT]
  R5 = Resistor [tolerance=±5% resistance=1k package=THT]
  S1 = Pushbutton [package="[THT]"]
  S2 = Pushbutton [package="[THT]"]
  R6 = Resistor [tolerance=±5% resistance=10k package=THT]
  R7 = Resistor [tolerance=±5% resistance=10k package=THT]
  C1 = Ceramic Capacitor [capacitance=100nF package="100 mil [THT, multilayer]"]
  C2 = Ceramic Capacitor [capacitance=100nF package="100 mil [THT, multilayer]"]

nets:
  N1: U1.3.3, R6.Pin_0, R7.Pin_0
  N2: U1.GPIO16, R4.Pin_0, R7.Pin_1, C1.0
  N3: U1.GPIO17, R5.Pin_0, R6.Pin_1, C2.0
  N4: U1.GPIO5, R2.Pin_1
  N5: U1.GPIO18, R1.Pin_1
  N6: U1.GPIO19, R3.Pin_1
  N7: U1.GND, LED1.cathode, LED2.cathode, LED3.cathode, S1.Pin_3, S1.Pin_4, S2.Pin_3, S2.Pin_4, C1.1, C2.1
  N8: LED1.anode, R3.Pin_0
  N9: LED2.anode, R1.Pin_0
  N10: LED3.anode, R2.Pin_0
  N11: R4.Pin_1, S2.Pin_1, S2.Pin_2
  N12: R5.Pin_1, S1.Pin_1, S1.Pin_2

custom parts:
  ESP32-38PinWide: Generic 38-Pin ESP32 with wide format (only access to one side of pins on a breadboard) based on Stephen Lilley's HiLetgo ESP-WROOM-32 ESP32 ESP-32S Development Board.
