# Fritzing sketch Devre6_KarasimsekKesmeler (saved by Fritzing 0.9.3b)
breadboards: 1

parts:
  U1 = ESP32-38PinWide [part_number=ESP32-38PinWide]
  LED1 = LED - 5mm [color="Red (633nm)" package="5 mm [THT]"]
  LED2 = LED - 5mm [color="Red (633nm)" package="5 mm [THT]"]
  LED3 = LED - 5mm [color="Red (633nm)" package="5 mm [THT]"]
  LED4 = LED - 5mm [color="Red (633nm)" package="5 mm [THT]"]
  LED5 = LED - 5mm [color="Red (633nm)" package="5 mm [THT]"]
  LED6 = LED - 5mm [color="Red (633nm)" package="5 mm [THT]"]
  LED7 = LED - 5mm [color="Red (633nm)" package="5 mm [THT]"]
  LED8 = LED - 5mm [color="Red (633nm)" package="5 mm [THT]"]
  S1 = Pushbutton [package="[THT]"]
  S2 = Pushbutton [package="[THT]"]

nets:
  N1: U1.GPIO32, S1.Pin_3, S1.Pin_4
  N2: U1.GPIO33, S2.Pin_3, S2.Pin_4
  N3: U1.GPIO16, LED8.anode
  N4: U1.GPIO17, LED2.anode
  N5: U1.GPIO5, LED3.anode
  N6: U1.GPIO19, LED4.anode
  N7: U1.GPIO21, LED5.anode
  N8: U1.GPIO22, LED6.anode
  N9: U1.GPIO23, LED1.anode
  N10: U1.GND, LED1.cathode, LED2.cathode, LED3.cathode, LED4.cathode, LED5.cathode, LED6.cathode, LED7.cathode, LED8.cathode, S1.Pin_1, S1.Pin_2, S2.Pin_1, S2.Pin_2

custom parts:
  ESP32-38PinWide: Generic 38-Pin ESP32 with wide format (only access to one side of pins on a breadboard) based on Stephen Lilley's HiLetgo ESP-WROOM-32 ESP32 ESP-32S Development Board.
