# Fritzing sketch Devre9_PWMHoparlor (saved by Fritzing 0.9.3b)
breadboards: 1

parts:
  U1 = ESP32-38PinWide [part_number=ESP32-38PinWide]
  SP1 = SPEAKER [package=pcb_mount_speaker]
  U2 = POT [package=pot_alpha_rv16af-20]

nets:
  N1: U1.3.3, U2.A
  N2: U1.GPIO34, U2.S
  N3: U1.GPIO14, SP1.-
  N4: U1.GPIO11, SP1.+
  N5: U1.GND, U2.E

custom parts:
  ESP32-38PinWide: Generic 38-Pin ESP32 with wide format (only access to one side of pins on a breadboard) based on Stephen Lilley's HiLetgo ESP-WROOM-32 ESP32 ESP-32S Development Board.
